# Fritzing sketch JammaDevBoard (saved by Fritzing 0.9.6b)
circuit board: 11.3cm x 6.5cm
breadboards: 1

parts:
  J5 = Jamma edge connector 2 [package=THT]
  Player_3 = DB9 Connector [package=db9]
  Player_4 = DB9 Connector [package=db9]
  Player_5 = DB9 Connector [package=db9]
  Player_6 = DB9 Connector [package=db9]
  GND = female pin header, 10 pins [form="♀ (female)"]
  +5V = female pin header, 10 pins [form="♀ (female)"]
  Player_7 = DB9 Connector [package=db9]
  Player_8 = DB9 Connector [package=db9]
  J6 = female pin header, 2 pins [form="♀ (female)"]
  Red = female pin header, 10 pins [form="♀ (female)"]
  Green = female pin header, 10 pins [form="♀ (female)"]
  Blue = female pin header, 10 pins [form="♀ (female)"]
  Sync = female pin header, 10 pins [form="♀ (female)"]
  VGND = female pin header, 10 pins [form="♀ (female)"]
  Part1 = SO08 [chip_label=SSOP16 package=SO]
  J8 = double row female pin header, 10 pins [form="♀ (female)"]
  J7 = double row female pin header, 10 pins [form="♀ (female)"]
  +12V = double row female pin header, 4 pins [form="♀ (female)"]
  J9 = female pin header, 2 pins [form="♀ (female)"]
  J10 = female pin header, 9 pins [form="♀ (female)"]
  J11 = female pin header, 9 pins [form="♀ (female)"]
  SVC = Resistor [tolerance=±5% power=0.25 resistance=220 package=THT]
  Test = Resistor [tolerance=±5% power=0.25 resistance=220 package=THT]
  Coin = Resistor [tolerance=±5% power=0.25 resistance=220 package=THT]
  Start = Resistor [tolerance=±5% power=0.25 resistance=220 package=THT]
  Up = Resistor [tolerance=±5% power=0.25 resistance=220 package=THT]
  Down = Resistor [tolerance=±5% power=0.25 resistance=220 package=THT]
  Left = Resistor [tolerance=±5% power=0.25 resistance=220 package=THT]
  Right = Resistor [tolerance=±5% power=0.25 resistance=220 package=THT]
  Bt1 = Resistor [tolerance=±5% power=0.25 resistance=220 package=THT]
  Bt2 = Resistor [tolerance=±5% power=0.25 resistance=220 package=THT]
  Bt3 = Resistor [tolerance=±5% power=0.25 resistance=220 package=THT]
  Down_2 = Resistor [tolerance=±5% power=0.25 resistance=220 package=THT]
  Bt3_2 = Resistor [tolerance=±5% power=0.25 resistance=220 package=THT]
  Right_2 = Resistor [tolerance=±5% power=0.25 resistance=220 package=THT]
  Bt1_2 = Resistor [tolerance=±5% power=0.25 resistance=220 package=THT]
  Coin_2 = Resistor [tolerance=±5% power=0.25 resistance=220 package=THT]
  Up_2 = Resistor [tolerance=±5% power=0.25 resistance=220 package=THT]
  Bt2_2 = Resistor [tolerance=±5% power=0.25 resistance=220 package=THT]
  Left_2 = Resistor [tolerance=±5% power=0.25 resistance=220 package=THT]
  Start_2 = Resistor [tolerance=±5% power=0.25 resistance=220 package=THT]
  Bt4 = Resistor [tolerance=±5% power=0.25 resistance=220 package=THT]
  Bt5 = Resistor [tolerance=±5% power=0.25 resistance=220 package=THT]
  Bt6 = Resistor [tolerance=±5% power=0.25 resistance=220 package=THT]
  Bt4_2 = Resistor [tolerance=±5% power=0.25 resistance=220 package=THT]
  Bt5_2 = Resistor [tolerance=±5% power=0.25 resistance=220 package=THT]
  Bt6_2 = Resistor [tolerance=±5% power=0.25 resistance=220 package=THT]
  USB = USB Connectors [package=usb-b-pth]
  J12 = double row female pin header, 4 pins [form="♀ (female)"]
  IC3 = MICROCONTROLLER [package=dil28-3]
  IC4 = MICROCONTROLLER [package=dil28-3]
  J15 = double row female pin header, 28 pins [form="♀ (female)"]
  J16 = double row female pin header, 28 pins [form="♀ (female)"]
  J18 = double row female pin header, 28 pins [form="♀ (female)"]
  J19 = double row female pin header, 28 pins [form="♀ (female)"]
  J20 = double row female pin header, 14 pins [form="♀ (female)"]  # not connected
  J17 = double row female pin header, 16 pins [form="♀ (female)"]  # not connected
  IC5 = Voltage Regulator [package=to220-igo]
  J21 = female pin header, 2 pins [form="♀ (female)"]
  C1 = Ceramic Capacitor [capacitance=100nF voltage=35V package="100 mil [THT, multilayer]"]
  C2 = Ceramic Capacitor [capacitance=100nF voltage=35V package="100 mil [THT, multilayer]"]
  Kicks = double row female pin header, 20 pins [form="♀ (female)"]

nets:
  N1: J5.pin1, J5.pin2, GND.pin1, GND.pin2, GND.pin3, GND.pin4, GND.pin5, GND.pin6, GND.pin7, GND.pin8, GND.pin9, GND.pin10
  N2: J5.pin3, J5.pin4, +5V.pin1, +5V.pin2, +5V.pin3, +5V.pin4, +5V.pin5, +5V.pin6, +5V.pin7, +5V.pin8, +5V.pin9, +5V.pin10
  N3: J5.pin6, J5.pin51, +12V.pin1, +12V.pin2, +12V.pin3, +12V.pin4, IC5.IN, C1.0
  N4: J5.pin10, J6.pin1
  N5: J5.pin12, Red.pin10
  N6: J5.pin13, Blue.pin10
  N7: J5.pin14, VGND.pin10
  N8: J5.pin15, J9.pin2, Test.Pin_1
  N9: J5.pin16, J10.pin9, Coin.Pin_1
  N10: J5.pin17, J10.pin8, Start.Pin_1
  N11: J5.pin18, J10.pin7, Up.Pin_1
  N12: J5.pin19, J10.pin6, Down.Pin_1
  N13: J5.pin20, J10.pin5, Left.Pin_1
  N14: J5.pin21, J10.pin4, Right.Pin_1
  N15: J5.pin22, J10.pin3, Bt1.Pin_1
  N16: J5.pin23, J10.pin2, Bt2.Pin_1
  N17: J5.pin24, J10.pin1, Bt3.Pin_1
  N18: J5.pin33, J11.pin1, Bt3_2.Pin_1
  N19: J5.pin34, J11.pin2, Bt2_2.Pin_1
  N20: J5.pin35, J11.pin3, Bt1_2.Pin_1
  N21: J5.pin36, J11.pin4, Right_2.Pin_1
  N22: J5.pin37, J11.pin5, Left_2.Pin_1
  N23: J5.pin38, J11.pin6, Down_2.Pin_1
  N24: J5.pin39, J11.pin7, Up_2.Pin_1
  N25: J5.pin40, J11.pin8, Start_2.Pin_1
  N26: J5.pin41, J11.pin9, Coin_2.Pin_1
  N27: J5.pin43, J9.pin1, SVC.Pin_1
  N28: J5.pin44, Sync.pin10
  N29: J5.pin45, Green.pin10
  N30: J5.pin47, J6.pin2
  N31: J5.pin53, J5.pin54
  N32: J5.pin55, J5.pin56, IC5.GND, C1.1, C2.0
  N33: Player_3.1, Player_5.1
  N34: Player_3.2, Player_5.2
  N35: Player_3.3, Player_5.3
  N36: Player_3.4, Player_5.4
  N37: Player_3.5, Player_5.5
  N38: Player_3.6, Player_5.6
  N39: Player_3.7, Player_5.7
  N40: Player_3.8, Player_5.8
  N41: Player_3.9, Player_5.9
  N42: Player_4.1, Player_6.1
  N43: Player_4.2, Player_6.2
  N44: Player_4.3, Player_6.3
  N45: Player_4.4, Player_6.4
  N46: Player_4.5, Player_6.5
  N47: Player_4.6, Player_6.6
  N48: Player_4.7, Player_6.7
  N49: Player_4.8, Player_6.8
  N50: Player_4.9, Player_6.9
  N51: Player_7.1, Player_8.1
  N52: Player_7.2, Player_8.2
  N53: Player_7.3, Player_8.3
  N54: Player_7.4, Player_8.4
  N55: Player_7.5, Player_8.5
  N56: Player_7.6, Player_8.6
  N57: Player_7.7, Player_8.7
  N58: Player_7.8, Player_8.8
  N59: Player_7.9, Player_8.9
  N60: Part1.1, J8.pin10
  N61: Part1.2, J8.pin9
  N62: Part1.3, J8.pin8
  N63: Part1.4, J8.pin7
  N64: Part1.5, J7.pin4
  N65: Part1.6, J7.pin3
  N66: Part1.7, J7.pin2
  N67: Part1.8, J7.pin1
  N68: SVC.Pin_0, Test.Pin_0, Coin.Pin_0, Start.Pin_0, Up.Pin_0, Down.Pin_0, Left.Pin_0, Right.Pin_0, Bt1.Pin_0, Bt2.Pin_0, Bt3.Pin_0, Down_2.Pin_0, Bt3_2.Pin_0, Right_2.Pin_0, Bt1_2.Pin_0, Coin_2.Pin_0, Up_2.Pin_0, Bt2_2.Pin_0, Left_2.Pin_0, Start_2.Pin_0, Bt4.Pin_1, Bt5.Pin_1, Bt6.Pin_1, Bt4_2.Pin_1, Bt5_2.Pin_1, Bt6_2.Pin_1
  N69: Bt4.Pin_0, Kicks.pin3, Kicks.pin18
  N70: Bt5.Pin_0, Kicks.pin4, Kicks.pin17
  N71: Bt6.Pin_0, Kicks.pin5, Kicks.pin16
  N72: Bt4_2.Pin_0, Kicks.pin7, Kicks.pin14
  N73: Bt5_2.Pin_0, Kicks.pin8, Kicks.pin13
  N74: Bt6_2.Pin_0, Kicks.pin9, Kicks.pin12
  N75: USB.D+, J12.pin1
  N76: USB.D-, J12.pin2
  N77: USB.GND, J12.pin4
  N78: USB.VBUS, J12.pin3
  N79: IC3.PC6(_RESET), J16.pin14
  N80: IC3.PD0(RXD), J16.pin13
  N81: IC3.PD1(TXD), J16.pin12
  N82: IC3.PD2(INT0), J16.pin11
  N83: IC3.PD3(INT1), J16.pin10
  N84: IC3.PD4(XCK_T0), J16.pin9
  N85: IC3.VCC, J16.pin8
  N86: IC3.GND, J16.pin7
  N87: IC3.PB6(XTAL1_TOSC1), J16.pin6
  N88: IC3.PB7(XTAL2_TOSC2), J16.pin5
  N89: IC3.PD5(T1), J16.pin4
  N90: IC3.PD6(AIN0), J16.pin3
  N91: IC3.PD7(AIN1), J16.pin2
  N92: IC3.PB0(ICP), J16.pin1
  N93: IC3.PB1(OC1A), J15.pin28
  N94: IC3.PB2(SS_OC1B), J15.pin27
  N95: IC3.PB3(MOSI_OC2), J15.pin26
  N96: IC3.PB4(MISO), J15.pin25
  N97: IC3.PB5(SCK), J15.pin24
  N98: IC3.AVCC, J15.pin23
  N99: IC3.AREF, J15.pin22
  N100: IC3.AGND, J15.pin21
  N101: IC3.PC0(ADC0), J15.pin20
  N102: IC3.PC1(ADC1), J15.pin19
  N103: IC3.PC2(ADC2), J15.pin18
  N104: IC3.PC3(ADC3), J15.pin17
  N105: IC3.PC4(ADC4_SDA), J15.pin16
  N106: IC3.PC5(ADC5_SCL), J15.pin15
  N107: IC4.PC6(_RESET), J19.pin14
  N108: IC4.PD0(RXD), J19.pin13
  N109: IC4.PD1(TXD), J19.pin12
  N110: IC4.PD2(INT0), J19.pin11
  N111: IC4.PD3(INT1), J19.pin10
  N112: IC4.PD4(XCK_T0), J19.pin9
  N113: IC4.VCC, J19.pin8
  N114: IC4.GND, J19.pin7
  N115: IC4.PB6(XTAL1_TOSC1), J19.pin6
  N116: IC4.PB7(XTAL2_TOSC2), J19.pin5
  N117: IC4.PD5(T1), J19.pin4
  N118: IC4.PD6(AIN0), J19.pin3
  N119: IC4.PD7(AIN1), J19.pin2
  N120: IC4.PB0(ICP), J19.pin1
  N121: IC4.PB1(OC1A), J18.pin28
  N122: IC4.PB2(SS_OC1B), J18.pin27
  N123: IC4.PB3(MOSI_OC2), J18.pin26
  N124: IC4.PB4(MISO), J18.pin25
  N125: IC4.PB5(SCK), J18.pin24
  N126: IC4.AVCC, J18.pin23
  N127: IC4.AREF, J18.pin22
  N128: IC4.AGND, J18.pin21
  N129: IC4.PC0(ADC0), J18.pin20
  N130: IC4.PC1(ADC1), J18.pin19
  N131: IC4.PC2(ADC2), J18.pin18
  N132: IC4.PC3(ADC3), J18.pin17
  N133: IC4.PC4(ADC4_SDA), J18.pin16
  N134: IC4.PC5(ADC5_SCL), J18.pin15
  N135: IC5.OUT, J21.pin1, C2.1

notes:
  Speaker+
  Speaker-
  Pull
  D+
  D-
  GND
  VBus
  Player 1
  Player 2
  Jamma Dev Board
  v1.0
  Player1
  Player2

custom parts:
  Jamma edge connector 2: PCB edge footprint for connecting Jamma dual 28pin connector
